# Fritzing sketch 数据转换模块电路文件 (saved by Fritzing 1.0.6)
breadboards: 1

parts:
  PSD = S1133 Si Photodiode [package="8mm Ceramic [THT]"]
  Arduino_UNO = Arduino Ethernet Shield (Rev3)
  ADS1115 = ADS1115
  R = Resistor [tolerance=±2% resistance=100000 package="2010 [SMD]"]
  Laser = LEDs [package=led10mm]
  VCC1 = Battery block 9V [internal_resistance=0.1Ω]
  AD8628 = DIP - 8 pins [chip_label=AD8628 package="DIP (Dual Inline) [THT]"]
  LED = smd LED [color="Yellow (592nm)" package="0603 [SMD]"]
  RL = Resistor [tolerance=±2% power=0.25W resistance=100000 package=THT]

nets (from the schematic view):
  GND: PSD.cathode, Arduino_UNO.GND, ADS1115.GND, ADS1115.ADDR, AD8628.V-, LED.cathode
  N1: PSD.anode, AD8628.+IN
  5V: Arduino_UNO.5V, ADS1115.VDD, AD8628.V+
  N2: Arduino_UNO.A4/SDA, ADS1115.SDA
  N3: Arduino_UNO.A5/SCL, ADS1115.SCL
  N4: Arduino_UNO.PWM_D6, RL.Pin_0
  N5: ADS1115.A0, R.Pin_0, AD8628.OUT
  N6: R.Pin_1, AD8628.-IN
  N7: Laser.C, VCC1.-
  N8: Laser.A, VCC1.+
  N9: LED.anode, RL.Pin_1

custom parts:
  ADS1115: ADC ADS1115
  DIP - 8 pins: A DIP stand-in part for whatever IC you want. With 8 pins on a 300mil dual inline package (DIP) footprint.
